# Fritzing sketch ZHAW_SimpleSafe Final (saved by Fritzing 1.0.6)
breadboards: 1

parts:
  RFID1 = RFID RC522 Module [package=THT]
  Part1 = Arduino Mega 2560 (Rev3)
  C1 = Electrolytic Capacitor [capacitance=0.1mF voltage=50V package="100 mil [THT, electrolytic]"]
  Keypad4x1 = Membran Keypad 4x4
  Gyroskop = InvenSense MPU6050
  LED1 = LED - 5mm [color="Red (633nm)" current=0.030A package="5 mm [THT]"]
  LED2 = LED - 5mm [color="Yellow (585nm)" current=30mA package="5 mm [THT]"]
  LED3 = LED - 5mm [color="Green (555nm)" current=0.030A package="5 mm [THT]"]
  R1 = Resistor [tolerance=±5% power=0.25W resistance=1k package=THT]
  R2 = Resistor [tolerance=±5% power=0.25W resistance=1k package=THT]
  R3 = Resistor [tolerance=±5% power=0.25W resistance=1k package=THT]
  M3 = Dagu DGServo 9g (Top view) [part_number=RS001B]
  LCD2004-I2C1 = LCD2004-I2C
  J1 = Piezo Speaker  # not connected

nets:
  N1: RFID1.NSS, Part1.D9_PWM
  N2: RFID1.SCK, Part1.D52
  N3: RFID1.MOSI, Part1.D51
  N4: RFID1.MISO, Part1.D50
  GND: RFID1.GND, Part1.GND, C1.-, Gyroskop.GND, LED1.cathode, LED2.cathode, LED3.cathode, M3.gnd, LCD2004-I2C1.GND
  N5: RFID1.RST, Part1.D8_PWM
  N6: Part1.D21/SCL, Gyroskop.SCL, LCD2004-I2C1.SCL
  N7: Part1.D20/SDA, Part1.SDA, Gyroskop.SDA, LCD2004-I2C1.SDA
  N8: Part1.D10_PWM, M3.pulse
  VCC: Part1.5V, Gyroskop.VCC, LCD2004-I2C1.VCC
  N9: Part1.D2_PWM, R3.Pin_1
  N10: Part1.D3_PWM, R2.Pin_1
  N11: Part1.D4_PWM, R1.Pin_1
  N12: Part1.D22, Keypad4x1.Pin1
  N13: Part1.D23, Keypad4x1.Pin2
  N14: Part1.D24, Keypad4x1.Pin3
  N15: Part1.D25, Keypad4x1.Pin4
  N16: Part1.D26, Keypad4x1.Pin5
  N17: Part1.D27, Keypad4x1.Pin6
  N18: Part1.D28, Keypad4x1.Pin7
  N19: Part1.D29, Keypad4x1.Pin8
  N20: C1.+, M3.vcc
  N21: LED1.anode, R1.Pin_0
  N22: LED2.anode, R2.Pin_0
  N23: LED3.anode, R3.Pin_0

notes:
  S2 = Button Tür geschlossen
  (optional)
  R6 = Photoresistor im Safe zur Diebstahlerkennung
  (optional)
  RST -> PWM8
  NSS -> PWM9
  R5 = Türposition
  (optional)
  KY-006 = Alarmanlage
  (optional)
  Gyroskop zur Diebstahlerkennung
  (optional)

custom parts:
  RFID RC522 Module: The RC522 is a 13.56MHz RFID module that is based on the MFRC522 controller from NXP semiconductors. The module can supports I2C, SPI and UART and normally is shipped with a RFID card and key fob. It is commonly used in attendance systems and other person/object identification applications.
  Membran Keypad 4x4: Membrane Keypad 4x4 Matrix
  LCD2004-I2C: A standard character display with 4x20 characters. Comes in many colors with LCM2004 IIC attached.
